// Logisim project state_transition.circ as structural Verilog: 3 circuits, main circuit main
module main (
);

  wire and_1_out, and_2_out, and_3_out, and_4_out, and_5_out, and_6_out, and_7_out, and_8_out, and_9_out,
       and_10_out, clock_1_out, decoder_1_out0, decoder_1_out4, decoder_1_out7, not_1_out, not_2_out,
       not_3_out, or_1_out, or_2_out, or_3_out;
  wire [2:0] d_ff_3_q;

  Clock clock_1 (.out(clock_1_out));
  D_Flip_Flop d_ff_1 (.clk(clock_1_out), .D(and_8_out), .Q(d_ff_3_q[2]), .en(1'b1));  // open: Qn, preset, reset
  D_Flip_Flop d_ff_2 (.clk(clock_1_out), .D(and_9_out), .Q(d_ff_3_q[1]), .en(1'b1));  // open: Qn, preset, reset
  D_Flip_Flop d_ff_3 (.clk(clock_1_out), .D(and_10_out), .Q(d_ff_3_q[0]), .en(1'b1));  // open: Qn, preset, reset
  Decoder #(.select(3), .enable("false")) decoder_1 (
    .out0(decoder_1_out0), .out4(decoder_1_out4), .out7(decoder_1_out7), .sel(d_ff_3_q));  // open: out1, out2, out3, out5, out6
  not not_1 (not_1_out, 1'b0);
  not not_2 (not_2_out, 1'b1);
  not not_3 (not_3_out, 1'b1);
  and and_1 (and_1_out, clock_1_out, or_1_out);
  or or_1 (or_1_out, decoder_1_out0, decoder_1_out4);
  and and_2 (and_2_out, 1'b1, 1'b1, 1'b1);
  and and_3 (and_3_out, 1'b1, 1'b1, 1'b0);
  and and_4 (and_4_out, 1'b1, 1'b1);
  and and_5 (and_5_out, 1'b1, 1'b0);
  and and_6 (and_6_out, 1'b1, 1'b1, not_1_out, not_3_out);
  or or_2 (or_2_out, and_2_out, and_3_out, and_7_out);
  and and_7 (and_7_out, 1'b1, not_2_out, not_1_out, not_3_out);
  Counter #(.width(4), .max('hf), .trigger("falling")) counter_1 (
    .clk(clock_1_out), .clr(and_1_out));  // open: load, D, count, Q, carry
  and and_8 (and_8_out, 1'b1, and_6_out);
  and and_9 (and_9_out, 1'b1, or_2_out);
  and and_10 (and_10_out, 1'b1, or_3_out);
  or or_3 (or_3_out, and_2_out, and_3_out, and_4_out, and_5_out);

  // Notes on the sheet:
  //   start
  //   RD/!WR
  //   TMAVL
  //   TMAVR
endmodule

module state_transition_opt (
);

  wire and_1_out, clock_1_out, d_ff_4_qn, decoder_1_out0, decoder_1_out1, decoder_1_out2, decoder_1_out3,
       decoder_1_out4, decoder_1_out5, nand_1_out, nand_2_out, nand_3_out, nand_4_out, nand_5_out,
       nand_6_out, nand_7_out, nand_8_out, nand_9_out, nand_10_out, nand_11_out, nand_12_out, nand_13_out,
       nand_14_out, nand_15_out, nand_16_out, nand_17_out, nand_18_out, nand_19_out, nand_20_out,
       nand_21_out, nor_1_out, nor_2_out, not_1_out, not_2_out, not_3_out, not_4_out, not_5_out, not_6_out,
       not_7_out, not_8_out, or_1_out, or_2_out;
  wire [2:0] d_ff_3_q;
  wire [3:0] counter_1_q;

  not not_1 (not_1_out, clock_1_out);
  Clock clock_1 (.out(clock_1_out));
  D_Flip_Flop d_ff_1 (.clk(not_1_out), .D(nand_12_out), .Q(d_ff_3_q[2]), .en(1'b1));  // open: Qn, preset, reset
  D_Flip_Flop d_ff_2 (.clk(not_1_out), .D(nand_18_out), .Q(d_ff_3_q[1]), .en(1'b1));  // open: Qn, preset, reset
  D_Flip_Flop d_ff_3 (.clk(not_1_out), .D(nand_19_out), .Q(d_ff_3_q[0]), .en(1'b1));  // open: Qn, preset, reset
  not not_2 (not_2_out, 1'b1);
  Counter #(.width(4), .max('hf)) counter_1 (
    .Q(counter_1_q), .clk(clock_1_out), .clr(or_1_out));  // open: load, D, count, carry
  Decoder #(.select(3), .enable("false")) decoder_1 (
    .out0(decoder_1_out0), .out1(decoder_1_out1), .out2(decoder_1_out2), .out3(decoder_1_out3),
    .out4(decoder_1_out4), .out5(decoder_1_out5), .sel(d_ff_3_q));  // open: out6, out7
  not not_3 (not_3_out, 1'b0);
  or or_1 (or_1_out, decoder_1_out0, decoder_1_out4);
  nand nand_1 (nand_1_out, 1'b1, clock_1_out);
  nand nand_2 (nand_2_out, 1'b1, 1'b0, 1'b0);
  nand nand_3 (nand_3_out, 1'b1, 1'b0, 1'b0);
  not not_4 (not_4_out, nor_1_out);
  nor nor_1 (nor_1_out, not_2_out, 1'b0, 1'b0, 1'b0);
  nand nand_4 (nand_4_out, 1'b1, 1'b0);
  nand nand_5 (nand_5_out, 1'b1, 1'b0);
  nand nand_6 (nand_6_out, nand_1_out, decoder_1_out0);
  and and_1 (and_1_out, counter_1_q[0], counter_1_q[1], counter_1_q[2], counter_1_q[3]);
  not not_5 (not_5_out, counter_1_q[1]);
  D_Flip_Flop #(.trigger("falling")) d_ff_4 (
    .clk(not_1_out), .D(counter_1_q[0]), .Qn(d_ff_4_qn));  // open: Q, preset, en, reset
  nor nor_2 (nor_2_out, 1'b0, 1'b0, not_3_out, not_2_out);
  nand nand_7 (nand_7_out, nand_2_out, nand_3_out, not_4_out);
  nand nand_8 (nand_8_out, nand_2_out, nand_3_out, nand_4_out, nand_5_out);
  nand nand_9 (nand_9_out, counter_1_q[0], counter_1_q[1], counter_1_q[2], counter_1_q[3]);
  not not_6 (not_6_out, decoder_1_out5);
  not not_7 (not_7_out, decoder_1_out4);
  nand nand_10 (nand_10_out, not_5_out, decoder_1_out1);
  nand nand_11 (nand_11_out, not_5_out, decoder_1_out2);
  nand nand_12 (nand_12_out, nand_13_out, nand_16_out, not_7_out);
  nand nand_13 (nand_13_out, decoder_1_out0, nor_2_out);
  nand nand_14 (nand_14_out, decoder_1_out0, nand_7_out);
  nand nand_15 (nand_15_out, decoder_1_out0, nand_8_out);
  nand nand_16 (nand_16_out, decoder_1_out5, nand_9_out);
  nand nand_17 (nand_17_out, decoder_1_out5, and_1_out);
  nand nand_18 (nand_18_out, nand_14_out, nand_17_out, nand_11_out);
  nand nand_19 (nand_19_out, nand_15_out, not_6_out, nand_10_out, not_7_out);
  or or_2 (or_2_out, decoder_1_out4, decoder_1_out5);
  not not_8 (not_8_out, decoder_1_out1);
  nand nand_20 (nand_20_out, d_ff_4_qn, counter_1_q[3]);
  nand nand_21 (nand_21_out, nand_20_out, not_8_out);

  // Notes on the sheet:
  //   start
  //   RD/!WR
  //   TMAVL
  //   TMAVR
  //   saves count(0) at rising clk edge
  //   Busy_and_A/Data/Rw_Latch
  //   count(0)_saved
  //   from_mem
  //   write_cache
  //   read_cache
  //   mem_enable
endmodule

module counter3 (
);

  wire button_1_out, clock_1_out, d_ff_1_q, d_ff_1_qn, d_ff_2_q, d_ff_2_qn, d_ff_3_q, d_ff_3_qn;

  Button button_1 (.out(button_1_out));
  D_Flip_Flop #(.trigger("falling")) d_ff_1 (
    .clk(d_ff_2_q), .D(d_ff_1_qn), .Q(d_ff_1_q), .Qn(d_ff_1_qn), .reset(button_1_out));  // open: preset, en
  Clock clock_1 (.out(clock_1_out));
  D_Flip_Flop #(.trigger("falling")) d_ff_2 (
    .clk(d_ff_3_q), .D(d_ff_2_qn), .Q(d_ff_2_q), .Qn(d_ff_2_qn), .reset(button_1_out));  // open: preset, en
  D_Flip_Flop #(.trigger("falling")) d_ff_3 (
    .clk(clock_1_out), .D(d_ff_3_qn), .Q(d_ff_3_q), .Qn(d_ff_3_qn), .reset(button_1_out));  // open: preset, en
endmodule
